# Fritzing sketch lamp (saved by Fritzing 0.5.2b)
breadboards: 1

parts:
  Teensy = Teensy 2.0
  10k = Resistor [resistance=10k package=THT]
  Q2 = NPN-Transistor [package="TO92 [THT]"]
  Q2_2 = NPN-Transistor [package="TO92 [THT]"]
  10k_2 = Resistor [resistance=10k package=THT]
  10k_3 = Resistor [resistance=10k package=THT]
  Q1 = NPN-Transistor [package="TO92 [THT]"]
  LED2 = RGB Common Cathode LED
  LED3 = RGB Common Cathode LED
  LED4 = RGB Common Cathode LED
  LED5 = RGB Common Cathode LED
  LED6 = RGB Common Cathode LED
  LED7 = RGB Common Cathode LED
  LED8 = RGB Common Cathode LED
  LED9 = RGB Common Cathode LED
  LED1 = RGB Common Cathode LED

nets:
  GND: Teensy.GND, LED2.connector1, LED3.connector1, LED4.connector1, LED5.connector1, LED6.connector1, LED7.connector1, LED8.connector1, LED9.connector1, LED1.connector1
  N1: Teensy.B7, 10k.Pin_0
  N2: Teensy.D0, 10k_2.Pin_0
  N3: Teensy.C7, 10k_3.Pin_0
  5V: Teensy.VCC, Q2.C, Q2_2.C, Q1.C
  N4: 10k.Pin_1, Q1.B
  N5: Q2.E, LED2.connector2, LED3.connector2, LED4.connector2, LED5.connector2, LED6.connector2, LED7.connector2, LED8.connector2, LED9.connector2, LED1.connector2
  N6: Q2.B, 10k_2.Pin_1
  N7: Q2_2.E, LED2.connector0, LED3.connector0, LED4.connector0, LED5.connector0, LED6.connector0, LED7.connector0, LED8.connector0, LED9.connector0, LED1.connector0
  N8: Q2_2.B, 10k_3.Pin_1
  N9: Q1.E, LED2.connector3, LED3.connector3, LED4.connector3, LED5.connector3, LED6.connector3, LED7.connector3, LED8.connector3, LED9.connector3, LED1.connector3
