# Fritzing sketch lamp (saved by Fritzing 0.5.2b)
breadboards: 1

parts:
  Teensy = Teensy 2.0
  10k = Resistor [resistance=10k package=THT]
  Q2 = NPN-Transistor [package="TO92 [THT]"]
  Q2_2 = NPN-Transistor [package="TO92 [THT]"]
  10k_2 = Resistor [resistance=10k package=THT]
  10k_3 = Resistor [resistance=10k package=THT]
  Q1 = NPN-Transistor [package="TO92 [THT]"]
  LED2 = RGB Common Cathode LED
  LED3 = RGB Common Cathode LED
  LED4 = RGB Common Cathode LED
  LED5 = RGB Common Cathode LED
  LED6 = RGB Common Cathode LED
  LED7 = RGB Common Cathode LED
  LED8 = RGB Common Cathode LED
  LED9 = RGB Common Cathode LED
  LED1 = RGB Common Cathode LED

nets:
  GND: Teensy.GND, LED2.Ground, LED3.Ground, LED4.Ground, LED5.Ground, LED6.Ground, LED7.Ground, LED8.Ground, LED9.Ground, LED1.Ground
  N1: Teensy.B7, 10k.Pin_0
  N2: Teensy.D0, 10k_2.Pin_0
  N3: Teensy.C7, 10k_3.Pin_0
  5V: Teensy.VCC, Q2.C, Q2_2.C, Q1.C
  N4: 10k.Pin_1, Q1.B
  N5: Q2.E, LED2.G_anode, LED3.G_anode, LED4.G_anode, LED5.G_anode, LED6.G_anode, LED7.G_anode, LED8.G_anode, LED9.G_anode, LED1.G_anode
  N6: Q2.B, 10k_2.Pin_1
  N7: Q2_2.E, LED2.R_anode, LED3.R_anode, LED4.R_anode, LED5.R_anode, LED6.R_anode, LED7.R_anode, LED8.R_anode, LED9.R_anode, LED1.R_anode
  N8: Q2_2.B, 10k_3.Pin_1
  N9: Q1.E, LED2.B_anode, LED3.B_anode, LED4.B_anode, LED5.B_anode, LED6.B_anode, LED7.B_anode, LED8.B_anode, LED9.B_anode, LED1.B_anode

custom parts:
  RGB Common Cathode LED: 5mm Common Cathode 4 pin RGB LED
